# Fritzing sketch Schema Arduino Mega 2560 (saved by Fritzing 0.9.2b)
circuit board: 8.46667cm x 5.64444cm
breadboards: 1

parts:
  Part1 = Arduino Mega 2560 (Rev3)
  U1 = ESP8266 WiFi Module [part_number=ESP8266]

nets:
  GND: Part1.D17_PWM/RX2, Part1.GND, U1.GPIO_2, U1.GND, U1.TXD
  N1: Part1.D16_PWM/TX2, U1.RXD
  3V3: Part1.3V3, U1.VCC, U1.RST, U1.CH_PD

custom parts:
  ESP8266 WiFi Module: Generic WiFi Module based on the ESP8266 with onboard PCB antenna and UART communications
